# Fritzing sketch beta_v0.0-2201 (saved by Fritzing 0.9.4)
circuit board: 8.46667cm x 5.64444cm
breadboards: 1

parts:
  ZS-042_RTC1 = ZS-042 RTC Module
  DHT22 = Humidity and Temperature Sensor RHT03
  USER_PUSH_BUTTON = SWITCH-MOMENTARY-2 [package=tactile-pth]
  R6 = Resistor [tolerance=±5% resistance=10k package="2512 [SMD]"]
  R1 = Resistor [tolerance=±5% resistance=1k package="2512 [SMD]"]
  22pF_CAPACITOR = Capacitor [package=cap-pth-small2]
  R7 = Resistor [tolerance=±5% resistance=4.7k package="0603 [SMD]"]
  ACCELEROMETER = ADXL335 [package=lfcsp-16]
  USER_LED1 = smd LED [color="Red (633nm)" package="0805 [SMD]"]
  R3 = Resistor [tolerance=±5% resistance=220 package="2512 [SMD]"]
  USER_LED3 = smd LED [color="Green (555nm)" package="0805 [SMD]"]
  R9 = Resistor [tolerance=±5% resistance=10k package="2512 [SMD]"]
  USER_LED2 = smd LED [color="Yellow (574nm)" package="0805 [SMD]"]
  U1 = atmega328 [package=dip]
  100uF_CAPACITOR = Capacitor Polarized [package=nippon_f80]
  XTAL = Crystal [frequency="16 Mhz" package=THT]
  microSD_module = MicroSD Card Module
  DC_INPUT_-_9V-12V = Power plug
  1000uF_CAPACITOR = Capacitor Polarized [package=cpol-radial-1000uf-25v]
  LM7805_Voltage_Regulator = Voltage Regulator [package=to-220-alt]
  R8 = Resistor [tolerance=±5% resistance=4.7k package="0603 [SMD]"]
  RESET_SWITCH = SWITCH-MOMENTARY-2 [package=tactile-pth-12mm]
  22pF_CAPACITOR_2 = Capacitor [package=cap-pth-small2]
  R4 = Resistor [tolerance=±5% resistance=220 package="2512 [SMD]"]
  R2 = Resistor [tolerance=±5% resistance=220 package="2512 [SMD]"]
  ON-OFF_SWITCH = SWITCH-SPST-2 [package=switch-spst-vertical]
  R5 = Resistor [tolerance=±5% resistance=10k package="2512 [SMD]"]
  16-BIT_ADC = Adafruit ADS1115 16Bit I2C ADC [part_number=ADC1115]

nets (from the schematic view):
  GND: ZS-042_RTC1.GND, DHT22.GND_2, 22pF_CAPACITOR.1, ACCELEROMETER.COM, USER_LED1.cathode, USER_LED3.cathode, USER_LED2.cathode, U1.GND, 100uF_CAPACITOR.-, microSD_module.GND, DC_INPUT_-_9V-12V.GND, 1000uF_CAPACITOR.-, LM7805_Voltage_Regulator.GND, RESET_SWITCH.1, 22pF_CAPACITOR_2.2, R5.Pin_1, 16-BIT_ADC.ADDR, 16-BIT_ADC.GND
  VCC: ZS-042_RTC1.VCC, USER_PUSH_BUTTON.2, R1.Pin_0, R7.Pin_1, ACCELEROMETER.VS, R9.Pin_1, U1.VCC, U1.AVCC, U1.AREF, 100uF_CAPACITOR.+, microSD_module.VCC, LM7805_Voltage_Regulator.OUT, R8.Pin_1, 16-BIT_ADC.VDD
  N1: ZS-042_RTC1.SDA, R7.Pin_0, U1.A4, 16-BIT_ADC.SDA
  N2: ZS-042_RTC1.SCL, U1.A5, R8.Pin_0, 16-BIT_ADC.SCL
  N3: DHT22.Vcc, R6.Pin_1
  N4: DHT22.Data-signal, R6.Pin_0, U1.D10_(PWM)
  N5: USER_PUSH_BUTTON.1, U1.D1_(TX), R5.Pin_0
  N6: R1.Pin_1, U1.RESET, RESET_SWITCH.2
  N7: 22pF_CAPACITOR.2, U1.XLAT2, XTAL.pin_1
  N8: ACCELEROMETER.YOUT, 16-BIT_ADC.AIN0
  N9: USER_LED1.anode, R4.Pin_0
  N10: R3.Pin_0, USER_LED2.anode
  N11: R3.Pin_1, U1.D5_(PWM)
  N12: USER_LED3.anode, R2.Pin_0
  N13: R9.Pin_0, U1.D3_(PWM), 16-BIT_ADC.ALERT
  N14: U1.D2, microSD_module.CS
  N15: U1.D4, R2.Pin_1
  N16: U1.XLAT1, XTAL.pin_0, 22pF_CAPACITOR_2.1
  N17: U1.D8, R4.Pin_1
  N18: U1.D11_(PWM), microSD_module.MOSI
  N19: U1.D12, microSD_module.MISO
  N20: U1.D13, microSD_module.SCK
  N21: DC_INPUT_-_9V-12V.VCC, ON-OFF_SWITCH.P
  N22: 1000uF_CAPACITOR.+, LM7805_Voltage_Regulator.IN, ON-OFF_SWITCH.O

custom parts:
  Humidity and Temperature Sensor RHT03: Digital relative humidity & temperature sensor RHT03
  MicroSD Card Module: A common microSD card module.
  Adafruit ADS1115 16Bit I2C ADC: For microcontrollers without an analog-to-digital converter or when you want a higher-precision ADC, the ADS1115 provides 16-bit precision at 860 samples/second over I2C. The chip can be configured as 4 single-ended input channels, or two differential channels. As a nice bonus, it even includes a programmable gain amplifier, up to x16, to help boost up smaller single/differential signals to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
