# Fritzing sketch 20210321_SCHEMATICS_v01 (saved by Fritzing 0.9.4)
circuit board: 10cm x 10cm
breadboards: 1

parts:
  DC_INPUT_-_9V-12V = Power plug
  XTAL = Crystal [frequency="16 Mhz" package=THT]
  22pF = Capacitor [package=cap-pth-small2]
  22pF_2 = Capacitor [package=cap-pth-small2]
  microSD = MicroSD Card Module
  We_need_to_solve_this_filter_problem_the_resistor_is_not_here = Capacitor Polarized [package=cpol-radial-1000uf-63v]
  ZS-042_RTC1 = ZS-042 RTC Module
  MOTOR1 = Header 2 [package=molex-1x2_lock]
  DHT22 = Header 3 [package=molex-1x3_lock]
  ACCEL_1 = Header 3 [package=molex-1x3_lock]
  ACCEL_2 = Header 3 [package=molex-1x3_lock]
  ACCEL_3 = Header 3 [package=molex-1x3_lock]
  ACCEL_4 = Header 3 [package=molex-1x3_lock]
  MOTOR2 = Header 2 [package=molex-1x2_lock]
  MOTOR3 = Header 2 [package=molex-1x2_lock]
  atMega328p = atmega328 [package=dip]
  R2 = Resistor [tolerance=±5% resistance=220 package=THT]
  R5 = Resistor [tolerance=±5% resistance=100 package=THT]
  R6 = Resistor [tolerance=±5% resistance=220 package=THT]
  R7 = Resistor [tolerance=±5% resistance=100 package=THT]
  R4 = Resistor [tolerance=±5% resistance=220 package=THT]
  R3 = Resistor [tolerance=±5% resistance=100 package=THT]
  R13 = Resistor [tolerance=±5% resistance=4.7k package=THT]
  R14 = Resistor [tolerance=±5% resistance=4.7k package=THT]
  10uF = Capacitor Polarized [package=cpol-radial-10uf-25v]
  10uF_2 = Capacitor Polarized [package=cpol-radial-10uf-25v]
  R15 = Resistor [tolerance=±5% resistance=220 package=THT]
  POWER_LED = Header 2 [package=molex-1x2_lock]
  PUSH_BUT = Header 2 [package=molex-1x2_lock]
  R8 = Resistor [tolerance=±5% resistance=10k package=THT]
  R12 = Resistor [tolerance=±5% resistance=10k package=THT]
  R10 = Resistor [tolerance=±5% resistance=220 package=THT]
  R9 = Resistor [tolerance=±5% resistance=220 package=THT]
  R11 = Resistor [tolerance=±5% resistance=220 package=THT]
  MOTOR4 = Header 2 [package=molex-1x2_lock]
  ON-OFF = Header 2 [package=molex-1x2_lock]
  16-BIT_ADC = Adafruit ADS1115 16Bit I2C ADC [part_number=ADC1115]
  RESET = Pushbutton [package="[THT]"]
  USRLD1 = Header 2 [package=molex-1x2_lock]
  USRLD2 = Header 2 [package=molex-1x2_lock]
  USRLD3 = Header 2 [package=molex-1x2_lock]
  LM7805 = Voltage Regulator [package=to220-igo]
  0_1uF = Capacitor [package=cap-pth-small2]
  0_1uF_2 = Capacitor [package=cap-pth-small2]
  R16 = Resistor [tolerance=±5% resistance=4.7k package=THT]
  J1 = female pin header, 3 pins [form="♀ (female)"]
  J2 = female pin header, 2 pins [form="♀ (female)"]
  R1 = Resistor [tolerance=±5% resistance=10k package=THT]
  0_1uF_3 = Capacitor [package=cap-pth-small2]
  J3 = female pin header, 4 pins [form="♀ (female)"]

nets:
  GND: DC_INPUT_-_9V-12V.GND, 22pF.2, 22pF_2.1, microSD.GND, We_need_to_solve_this_filter_problem_the_resistor_is_not_here.-, ZS-042_RTC1.GND#0, MOTOR1.1, DHT22.1, ACCEL_1.3, ACCEL_2.3, ACCEL_3.3, ACCEL_4.3, MOTOR2.1, MOTOR3.1, atMega328p.GND, R2.Pin_0, R6.Pin_0, R4.Pin_0, 10uF.-, 10uF_2.-, POWER_LED.1, R12.Pin_1, MOTOR4.1, 16-BIT_ADC.ADDR, 16-BIT_ADC.GND, RESET.Pin_1, RESET.Pin_2, USRLD1.1, USRLD2.1, USRLD3.1, LM7805.GND, 0_1uF.1, 0_1uF_2.2, J1.pin2
  N1: DC_INPUT_-_9V-12V.VCC, ON-OFF.1
  N2: XTAL.pin_0, 22pF.1, atMega328p.XLAT1
  N3: XTAL.pin_1, 22pF_2.2, atMega328p.XLAT2
  VCC: microSD.VCC, We_need_to_solve_this_filter_problem_the_resistor_is_not_here.+, ZS-042_RTC1.VCC#1, DHT22.2, ACCEL_1.2, ACCEL_2.2, ACCEL_3.2, ACCEL_4.2, atMega328p.VCC, atMega328p.AVCC, atMega328p.AREF, R13.Pin_0, R14.Pin_1, 10uF_2.+, R15.Pin_1, PUSH_BUT.1, R8.Pin_0, 16-BIT_ADC.VDD, LM7805.OUT, 0_1uF.2, 0_1uF_2.1, R16.Pin_1, J1.pin3, R1.Pin_0
  N4: microSD.MISO, atMega328p.D6_(PWM)
  N5: microSD.MOSI, R2.Pin_1, R3.Pin_0
  N6: microSD.SCK, R5.Pin_0, R4.Pin_1
  N7: microSD.CS, R6.Pin_1, R7.Pin_0
  N8: ZS-042_RTC1.SDA#2, atMega328p.A4, R13.Pin_1, 16-BIT_ADC.SDA
  N9: ZS-042_RTC1.SCL#3, atMega328p.A5, R14.Pin_0, 16-BIT_ADC.SCL
  N10: ZS-042_RTC1.SQW, atMega328p.D13, R16.Pin_0
  N11: ZS-042_RTC1.GND#6, J3.pin4
  N12: ZS-042_RTC1.VCC#7, J3.pin3
  N13: ZS-042_RTC1.SDA#8, J3.pin2
  N14: ZS-042_RTC1.SCL#9, J3.pin1
  N15: MOTOR1.2, atMega328p.D9_(PWM)
  N16: DHT22.3, atMega328p.D12, R8.Pin_1
  N17: ACCEL_1.1, 16-BIT_ADC.AIN0
  N18: ACCEL_2.1, 16-BIT_ADC.AIN1
  N19: ACCEL_3.1, 16-BIT_ADC.AIN2
  N20: ACCEL_4.1, 16-BIT_ADC.AIN3
  N21: MOTOR2.2, atMega328p.D10_(PWM)
  N22: MOTOR3.2, atMega328p.D11_(PWM)
  N23: atMega328p.RESET, RESET.Pin_3, RESET.Pin_4, R1.Pin_1, 0_1uF_3.2
  N24: atMega328p.D0_(RX), R11.Pin_1, J2.pin1
  N25: atMega328p.D1_(TX), PUSH_BUT.2, R12.Pin_0, J2.pin2
  N26: atMega328p.D2, R7.Pin_1
  N27: atMega328p.D3_(PWM), MOTOR4.2
  N28: atMega328p.D4, R10.Pin_1
  N29: atMega328p.D5_(PWM), R3.Pin_1
  N30: atMega328p.D7, R5.Pin_1
  N31: atMega328p.D8, R9.Pin_1
  N32: 10uF.+, ON-OFF.2, LM7805.IN
  N33: R15.Pin_0, POWER_LED.2
  N34: R10.Pin_0, USRLD2.2
  N35: R9.Pin_0, USRLD1.2
  N36: R11.Pin_0, USRLD3.2
  N37: J1.pin1, 0_1uF_3.1

notes:
  GND
  VCC
  MISO
  MOSI
  SCK
  CS
  UNIVERSIDADE DE BRASILIA
  DEPARTAMENTO DE ENGENHARIA CIVIL E AMBIENTAL
  EMM-ARM
  Elastic Modulus Measurement through Ambient Response Method
  POS GRADUACAO EM ESTRUTURAS E CONSTRUCAO CIVIL
  Sistema de automacao para ensaio
  Renan Rocha Ribeiro (renan.rocha.ribeiro@gmail.com)
  Rodrigo Lameiras (rmlameiras@gmail.com)
  Versao beta - 0.1
  22/02/2021
  -
  +
  RX
  TX
  RTS

custom parts:
  MicroSD Card Module: A common microSD card module.
  Adafruit ADS1115 16Bit I2C ADC: For microcontrollers without an analog-to-digital converter or when you want a higher-precision ADC, the ADS1115 provides 16-bit precision at 860 samples/second over I2C. The chip can be configured as 4 single-ended input channels, or two differential channels. As a nice bonus, it even includes a programmable gain amplifier, up to x16, to help boost up smaller single/differential signals to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
