# Fritzing sketch 20210421_microEMMARM_v00 (saved by Fritzing 0.9.4)
circuit board: 8.46667cm x 5.64444cm
breadboards: 1

parts:
  U1 = atmega328 [package=dip]
  LM7805_Voltage_Regulator = Voltage Regulator [package=to-220-alt]
  100uF_CAPACITOR = Capacitor Polarized [package=nippon_f80]
  1000uF_CAPACITOR = Capacitor Polarized [package=cpol-radial-1000uf-25v]
  DC_INPUT_-_9V-12V = Power plug
  ON-OFF_SWITCH = SWITCH-SPST-2 [package=switch-spst-vertical]
  XTAL = Crystal [frequency="16 Mhz" package=THT]
  22pF_CAPACITOR = Capacitor [package=cap-pth-small2]
  22pF_CAPACITOR_2 = Capacitor [package=cap-pth-small2]
  R1 = Resistor [tolerance=±5% resistance=1k package="2512 [SMD]"]
  RESET_SWITCH = SWITCH-MOMENTARY-2 [package=tactile-pth-12mm]
  R2 = Resistor [tolerance=±5% resistance=220 package="2512 [SMD]"]
  microSD2 = MicroSD Card Module
  R3 = Resistor [tolerance=±5% resistance=100 package="2512 [SMD]"]
  R4 = Resistor [tolerance=±5% resistance=220 package="2512 [SMD]"]
  R5 = Resistor [tolerance=±5% resistance=100 package="2512 [SMD]"]
  R6 = Resistor [tolerance=±5% resistance=220 package="2512 [SMD]"]
  R7 = Resistor [tolerance=±5% resistance=100 package="2512 [SMD]"]
  1000uF_CAPACITOR_2 = Capacitor Polarized [package=cpol-radial-1000uf-63v]
  ADXL335_ACCELEROMETER = ADXL335 [package=lfcsp-16]
  ZS-042_RTC1 = ZS-042 RTC Module
  16-BIT_ADC = Adafruit ADS1115 16Bit I2C ADC [part_number=ADC1115]
  USER_LED1 = smd LED [color="Red (633nm)" package="0805 [SMD]"]
  USER_LED2 = smd LED [color="Yellow (574nm)" package="0805 [SMD]"]
  USER_LED3 = smd LED [color="Green (555nm)" package="0805 [SMD]"]
  R9 = Resistor [tolerance=±5% resistance=220 package="2512 [SMD]"]
  R10 = Resistor [tolerance=±5% resistance=220 package="2512 [SMD]"]
  R11 = Resistor [tolerance=±5% resistance=220 package="2512 [SMD]"]
  USER_PUSH_BUTTON = SWITCH-MOMENTARY-2 [package=tactile-pth]
  R12 = Resistor [tolerance=±5% resistance=10k package="2512 [SMD]"]
  R8 = Resistor [tolerance=±5% resistance=10k package="2512 [SMD]"]
  DHT22 = Humidity and Temperature Sensor RHT03
  R13 = Resistor [tolerance=±5% resistance=4.7k package="0603 [SMD]"]
  R14 = Resistor [tolerance=±5% resistance=4.7k package="0603 [SMD]"]

nets (from the schematic view):
  N1: U1.RESET, R1.Pin_1, RESET_SWITCH.2
  N2: U1.D1_(TX), USER_PUSH_BUTTON.1, R12.Pin_0
  N3: U1.D2, R7.Pin_1
  N4: U1.D3_(PWM), R11.Pin_1
  N5: U1.D4, R10.Pin_1
  VCC: U1.VCC, U1.AVCC, U1.AREF, LM7805_Voltage_Regulator.OUT, 100uF_CAPACITOR.+, R1.Pin_0, microSD2.VCC, 1000uF_CAPACITOR_2.-, ADXL335_ACCELEROMETER.VS, ZS-042_RTC1.VCC, 16-BIT_ADC.VDD, USER_PUSH_BUTTON.2, R13.Pin_1, R14.Pin_1
  GND: U1.GND, LM7805_Voltage_Regulator.GND, 100uF_CAPACITOR.-, 1000uF_CAPACITOR.-, DC_INPUT_-_9V-12V.GND, 22pF_CAPACITOR.2, 22pF_CAPACITOR_2.1, RESET_SWITCH.1, R2.Pin_0, microSD2.GND, R4.Pin_0, R6.Pin_0, 1000uF_CAPACITOR_2.+, ADXL335_ACCELEROMETER.COM, ZS-042_RTC1.GND, 16-BIT_ADC.ADDR, 16-BIT_ADC.GND, USER_LED1.cathode, USER_LED2.cathode, USER_LED3.cathode, R12.Pin_1, DHT22.GND_2
  N6: U1.XLAT1, XTAL.pin_0, 22pF_CAPACITOR.1
  N7: U1.XLAT2, XTAL.pin_1, 22pF_CAPACITOR_2.2
  N8: U1.D5_(PWM), R3.Pin_1
  N9: U1.D6_(PWM), microSD2.MISO
  N10: U1.D7, R5.Pin_1
  N11: U1.D8, R9.Pin_1
  N12: U1.D13, R8.Pin_0, DHT22.Data-signal
  N13: U1.A4, ZS-042_RTC1.SDA, 16-BIT_ADC.SDA, R14.Pin_0
  N14: U1.A5, ZS-042_RTC1.SCL, 16-BIT_ADC.SCL, R13.Pin_0
  N15: LM7805_Voltage_Regulator.IN, 1000uF_CAPACITOR.+, ON-OFF_SWITCH.O
  N16: DC_INPUT_-_9V-12V.VCC, ON-OFF_SWITCH.P
  N17: R2.Pin_1, microSD2.MOSI, R3.Pin_0
  N18: microSD2.SCK, R4.Pin_1, R5.Pin_0
  N19: microSD2.CS, R6.Pin_1, R7.Pin_0
  N20: ADXL335_ACCELEROMETER.YOUT, 16-BIT_ADC.AIN0
  N21: USER_LED1.anode, R9.Pin_0
  N22: USER_LED2.anode, R10.Pin_0
  N23: USER_LED3.anode, R11.Pin_0
  N24: R8.Pin_1, DHT22.Vcc

custom parts:
  MicroSD Card Module: A common microSD card module.
  Adafruit ADS1115 16Bit I2C ADC: For microcontrollers without an analog-to-digital converter or when you want a higher-precision ADC, the ADS1115 provides 16-bit precision at 860 samples/second over I2C. The chip can be configured as 4 single-ended input channels, or two differential channels. As a nice bonus, it even includes a programmable gain amplifier, up to x16, to help boost up smaller single/differential signals to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
  Humidity and Temperature Sensor RHT03: Digital relative humidity & temperature sensor RHT03
