# Fritzing sketch 20221118_SCHEMATICS-COMPLETE (saved by Fritzing 0.9.10b)
circuit board: 10cm x 10cm
breadboards: 4

parts:
  #P39 = Power plug
  #P09 = Crystal [frequency="16 Mhz" package=THT]
  #P06 = Capacitor [package=cap-pth-small2]
  #P15 = atmega328 [package=dip]
  #P19 = Resistor [tolerance=±5% resistance=4.7k power=0.25 package=THT]
  #P20 = Resistor [tolerance=±5% resistance=4.7k power=0.25 package=THT]
  #P32 = Capacitor Polarized [package=cpol-radial-10uf-25v]
  #P18 = Capacitor Polarized [package=cpol-radial-10uf-25v]
  #P17 = Resistor [tolerance=±5% resistance=220 power=0.25 package=THT]
  #P35 = Resistor [tolerance=±5% resistance=10k power=0.25 package=THT]
  #P36 = Resistor [tolerance=±5% resistance=10k power=0.25 package=THT]
  #P26 = Resistor [tolerance=±5% resistance=220 power=0.25 package=THT]
  #P23 = Resistor [tolerance=±5% resistance=220 power=0.25 package=THT]
  #P30 = Resistor [tolerance=±5% resistance=220 power=0.25 package=THT]
  #P01 = Adafruit ADS1115 16Bit I2C ADC [part_number=ADC1115]
  #P10 = Pushbutton [package="[THT]"]
  #P25 = Voltage Regulator [package=to220-igo]
  #P22 = Capacitor [package=cap-pth-small2]
  #P11 = Capacitor [package=cap-pth-small2]
  #P12 = Resistor [tolerance=±5% resistance=10k power=0.25 package=THT]
  #P13 = Capacitor [package=cap-pth-small2]
  #P08 = molex pin header, 6 pins [form=molex]
  #P14 = molex pin header, 2 pins [form=molex]
  DS3231_RTC = ZS-042 RTC Module
  #P16 = molex pin header, 5 pins [form=molex]
  #P41 = molex pin header, 4 pins [form=molex]
  #P24 = molex pin header, 2 pins [form=molex]
  #P27 = molex pin header, 2 pins [form=molex]
  #P31 = molex pin header, 2 pins [form=molex]
  #P02 = molex pin header, 3 pins [form=molex]
  #P03 = molex pin header, 3 pins [form=molex]
  #P04 = molex pin header, 3 pins [form=molex]
  #P05 = molex pin header, 3 pins [form=molex]
  #P40 = molex pin header, 2 pins [form=molex]
  #P38 = molex pin header, 2 pins [form=molex]
  #P28 = molex pin header, 2 pins [form=molex]
  #P29 = molex pin header, 2 pins [form=molex]
  #P33 = molex pin header, 2 pins [form=molex]
  #P34 = molex pin header, 2 pins [form=molex]
  #P37 = molex pin header, 3 pins [form=molex]
  #P07 = Capacitor [package=cap-pth-small2]
  GND = female pin header, 1 pin [form="♀ (female)"]

nets:
  GND: #P39.GND, #P06.1, #P15.GND, #P32.-, #P18.-, #P36.Pin_1, #P01.ADDR, #P01.GND, #P10.Pin_1, #P10.Pin_2, #P25.GND, #P22.1, #P11.2, #P08.pin1, #P14.pin2, DS3231_RTC.GND#0, #P16.pin3, #P24.pin2, #P27.pin2, #P31.pin2, #P02.pin1, #P03.pin1, #P04.pin1, #P05.pin1, #P28.pin2, #P29.pin2, #P33.pin2, #P34.pin2, #P37.pin3, #P07.2, GND.pin1
  N1: #P39.VCC, #P40.pin2
  XTAL_1: #P09.pin_0, #P15.XLAT1, #P07.1
  XTAL_2: #P09.pin_1, #P06.2, #P15.XLAT2
  RST: #P15.RESET, #P10.Pin_3, #P10.Pin_4, #P12.Pin_1, #P13.2
  RX: #P15.D0_(RX), #P16.pin5
  TX: #P15.D1_(TX), #P16.pin1
  CS: #P15.D2, #P08.pin6
  ALRT: #P15.D3_(PWM), #P01.ALERT
  PLUS_BUT: #P15.D4, #P26.Pin_1
  VCC: #P15.VCC, #P15.AVCC, #P15.AREF, #P19.Pin_0, #P20.Pin_1, #P18.+, #P17.Pin_1, #P35.Pin_0, #P01.VDD, #P25.OUT, #P22.2, #P11.1, #P12.Pin_0, #P08.pin2, DS3231_RTC.VCC#1, #P16.pin2, #P02.pin2, #P03.pin2, #P04.pin2, #P05.pin2, #P38.pin2, #P37.pin2
  ARROW_BUT: #P15.D5_(PWM), #P30.Pin_1
  MINUS_BUT: #P15.D8, #P23.Pin_1
  PAUSE_BUT: #P15.D9_(PWM), #P36.Pin_0, #P38.pin1
  DHT_DATA: #P15.D10_(PWM), #P35.Pin_1, #P37.pin1
  MOSI: #P15.D11_(PWM), #P08.pin4
  MISO: #P15.D12, #P08.pin3
  SCK: #P15.D13, #P08.pin5
  A0: #P15.A0, #P28.pin1
  A1: #P15.A1, #P33.pin1
  A2: #P15.A2, #P34.pin1
  A3: #P15.A3, #P29.pin1
  SDA: #P15.A4, #P19.Pin_1, #P01.SDA, DS3231_RTC.SDA#2
  SCL: #P15.A5, #P20.Pin_0, #P01.SCL, DS3231_RTC.SCL#3
  N2: #P32.+, #P25.IN, #P40.pin1
  N3: #P17.Pin_0, #P14.pin1
  N4: #P26.Pin_0, #P27.pin1
  N5: #P23.Pin_0, #P24.pin1
  N6: #P30.Pin_0, #P31.pin1
  AIN3: #P01.AIN3, #P02.pin3
  AIN2: #P01.AIN2, #P03.pin3
  AIN1: #P01.AIN1, #P04.pin3
  AIN0: #P01.AIN0, #P05.pin3
  N7: #P13.1, #P16.pin4
  N8: DS3231_RTC.GND#6, #P41.pin4
  N9: DS3231_RTC.VCC#7, #P41.pin3
  N10: DS3231_RTC.SDA#8, #P41.pin2
  N11: DS3231_RTC.SCL#9, #P41.pin1

notes:
  GND
  VCC
  MISO
  MOSI
  SCK
  CS
  POS GRADUACAO EM ESTRUTURAS E CONSTRUCAO CIVIL
  University of Brasilia
  Sistema de automacao para ensaio
  Renan Rocha Ribeiro - 03/11/2022
  -
  +
  RX
  TX
  RST
  SDA
  SCL
  SQW
  32K
  AI3
  AI2
  AI1
  AI0
  ALRT
  ADDR
  University of Minho
  renan.rocha.ribeiro@gmail.com
  9V-12V
  LCD SCREEN
  D
  INP
  5V
  microSD module
  ON/OFF BUTTON
  #P21a
  DS3231
  #P21b
  DATA
  ADS1115 module
  ATmega328p
  CP2102 for USB/Serial
  - button
  A0
  A3
  A1
  A2
  D1
  D4
  D2
  D3
  + button
  -> button
  ⏸ button
  #P21a & 21b

custom parts:
  Adafruit ADS1115 16Bit I2C ADC: For microcontrollers without an analog-to-digital converter or when you want a higher-precision ADC, the ADS1115 provides 16-bit precision at 860 samples/second over I2C. The chip can be configured as 4 single-ended input channels, or two differential channels. As a nice bonus, it even includes a programmable gain amplifier, up to x16, to help boost up smaller single/differential signals to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
